// Logisim project Circuit.circ as structural Verilog: 1 circuit, main circuit main
module main (
  input  [7:0] in_1,
  input  [7:0] in_2,
  input  [7:0] in_3,
  output out_4,
  output out_5
);

  wire xor_1_out, xor_2_out, xor_3_out, xor_4_out, xor_5_out, xor_6_out, xor_7_out, xor_8_out, xor_9_out,
       xor_10_out, xor_11_out, xor_12_out, xor_14_out;
  wire [7:0] register_1_q;

  Register register_1 (.D(in_3), .Q(register_1_q));  // open: en, clk, clr
  xor xor_1 (xor_1_out, in_1[0], in_1[1]);
  xor xor_2 (xor_2_out, in_1[2], in_1[3]);
  xor xor_3 (xor_3_out, in_1[4], in_1[5]);
  xor xor_4 (xor_4_out, in_1[6], in_1[7]);
  xor xor_5 (xor_5_out, in_2[0], in_2[1]);
  xor xor_6 (xor_6_out, in_2[2], in_2[3]);
  xor xor_7 (xor_7_out, in_2[4], in_2[5]);
  xor xor_8 (xor_8_out, in_2[6], in_2[7]);
  xor xor_9 (xor_9_out, xor_1_out, xor_2_out);
  xor xor_10 (xor_10_out, xor_3_out, xor_4_out);
  xor xor_11 (xor_11_out, xor_5_out, xor_6_out);
  xor xor_12 (xor_12_out, xor_7_out, xor_8_out);
  xor xor_13 (out_4, xor_9_out, xor_10_out);
  xor xor_14 (xor_14_out, xor_11_out, xor_12_out);
  not not_1 (out_5, xor_14_out);
endmodule
