// Logisim project gates.circ as structural Verilog: 1 circuit, main circuit main
module main (
  input  in_1,
  input  input_1,
  input  in_3,
  input  in_4,
  input  a,
  input  b,
  input  carry,
  input  a_2,
  input  b_2,
  input  carry_2,
  output out_11,
  output sum___a_XOR_b,
  output out_13,
  output sum,
  output carry_out,
  output difference,
  output carry_out_2
);

  wire and_1_out, and_2_out, and_3_out, and_4_out, not_1_out, not_2_out, not_3_out, xor_2_out, xor_3_out;

  not not_1 (not_1_out, a_2);
  xor xor_1 (sum___a_XOR_b, input_1, in_4);
  xor xor_2 (xor_2_out, a, b);
  and and_1 (and_1_out, a, b);
  xor xor_3 (xor_3_out, a_2, b_2);
  and and_2 (and_2_out, not_1_out, b_2);
  not not_2 (not_2_out, xor_3_out);
  xor xor_4 (sum, xor_2_out, carry);
  and and_3 (and_3_out, xor_2_out, carry);
  and and_4 (and_4_out, not_2_out, carry_2);
  or or_1 (carry_out, and_1_out, and_3_out);
  xor xor_5 (difference, xor_3_out, carry_2);
  or or_2 (carry_out_2, and_2_out, and_4_out);
  not not_3 (not_3_out, in_1);
  xor xor_6 (out_11, in_1, in_3);
  and and_5 (out_13, not_3_out, in_3);

  // Notes on the sheet:
  //   input 2
  //   full adder
  //   full subtractor
  //   1 bit half adder
  //   1 bit full adder
  //   1 bit half adder
endmodule
