// Logisim project Circuit1.circ as structural Verilog: 1 circuit, main circuit main
module main (
  input  I0,
  input  I1,
  input  I2,
  input  I3,
  output O1,
  output Output_2
);

  wire not_1_out, not_2_out, not_3_out, xor_1_out, xor_2_out;

  not not_1 (not_1_out, I0);
  not not_2 (not_2_out, I1);
  not not_3 (not_3_out, I2);
  xor xor_1 (xor_1_out, I1, I3);
  xor xor_2 (xor_2_out, I2, I3);
  and and_1 (O1, xor_1_out, not_1_out, not_3_out);
  and and_2 (Output_2, xor_2_out, not_1_out, not_2_out);

  // Notes on the sheet:
  //   .
  //   1.Design a circuit for 4-2 encoder.
  //   Output 1
  //   O0
endmodule
