// Logisim project Circuit2.circ as structural Verilog: 1 circuit, main circuit main
module main (
  input  I2,
  input  I1,
  input  I0,
  output Output_1,
  output Output_2,
  output Output_3,
  output Output_4,
  output Output_5,
  output out_9,
  output Output_7,
  output Output_8
);

  wire not_1_out, not_2_out, not_3_out;

  not not_1 (not_1_out, I2);
  not not_2 (not_2_out, I1);
  not not_3 (not_3_out, I0);
  and and_1 (Output_1, not_1_out, not_2_out, not_3_out);
  and and_2 (Output_2, not_1_out, not_2_out, I0);
  and and_3 (Output_3, not_1_out, I1, not_3_out);
  and and_4 (Output_4, not_1_out, I1, I0);
  and and_5 (Output_5, I2, not_2_out, not_3_out);
  and and_6 (out_9, I2, not_2_out, I0);
  and and_7 (Output_7, I2, I1, not_3_out);
  and and_8 (Output_8, I2, I1, I0);

  // Notes on the sheet:
  //   3.Design 3 to 8 Decoder
  //   Output 1
  //   Output 2
  //   Output 3
  //   Output 4
  //   Output 5
  //   Output 6
  //   Output 6
  //   Output 7
  //   Output 8
endmodule
