// Logisim project Circuit3.circ as structural Verilog: 1 circuit, main circuit main
module main (
  input  [7:0] in_1,
  input  [7:0] in_2,
  output out_3,
  output out_4,
  output out_5
);

  Comparator comparator_1 (.a(in_1), .b(in_2), .gt(out_3), .eq(out_4), .lt(out_5));
  Comparator comparator_2 ();  // open: a, b, gt, eq, lt

  // Notes on the sheet:
  //   3.Design a circuit that compares Two Eight Bit Numbers.
  //   First input is greater
  //   Second input is greater
  //   Equal inputs
endmodule
