// Logisim project Circuit4.circ as structural Verilog: 1 circuit, main circuit main
module main (
  input  S1,
  input  S0,
  input  I0,
  input  I1,
  input  Enable,
  input  I2,
  input  I3,
  output out_8
);

  wire and_1_out, and_2_out, and_3_out, and_4_out, not_1_out, not_2_out, or_1_out;

  not not_1 (not_1_out, S1);
  not not_2 (not_2_out, S0);
  and and_1 (and_1_out, I0, not_2_out, not_1_out);
  and and_2 (and_2_out, I1, S0, not_1_out);
  and and_3 (and_3_out, I2, not_2_out, S1);
  and and_4 (and_4_out, I3, S0, S1);
  or or_1 (or_1_out, and_1_out, and_2_out, and_3_out, and_4_out);
  and and_5 (out_8, or_1_out, Enable);

  // Notes on the sheet:
  //   4. Design ALU circuit contains basic operations using multiplexers.
endmodule
