// Logisim project Circuit5.circ as structural Verilog: 1 circuit, main circuit main
module main (
  input  [7:0] in_1,
  input  in_2,
  input  in_3,
  input  in_4,
  input  in_5,
  input  in_6,
  input  in_7,
  input  in_8,
  input  in_9,
  output [3:0] out_10,
  output out_11,
  output out_12,
  output out_13,
  output out_14
);

  wire not_1_out, not_2_out, not_3_out, not_4_out, not_5_out, not_6_out, xor_1_out, xor_2_out, xor_3_out,
       xor_4_out;

  not not_1 (not_1_out, in_2);
  not not_2 (not_2_out, in_6);
  not not_3 (not_3_out, in_3);
  not not_4 (not_4_out, in_4);
  not not_5 (not_5_out, in_7);
  not not_6 (not_6_out, in_8);
  assign out_10 = in_1[3:0] & in_1[7:4];  // AND_Gate and_1, 4 bits wide
  xor xor_1 (xor_1_out, in_3, in_5);
  xor xor_2 (xor_2_out, in_7, in_9);
  xor xor_3 (xor_3_out, in_4, in_5);
  xor xor_4 (xor_4_out, in_8, in_9);
  and and_2 (out_11, xor_1_out, not_1_out, not_4_out);
  and and_3 (out_13, xor_3_out, not_1_out, not_3_out);
  and and_4 (out_12, xor_2_out, not_2_out, not_6_out);
  and and_5 (out_14, xor_4_out, not_2_out, not_5_out);

  // Notes on the sheet:
  //   8 bit input
  //   5. Split 8 bits into 2 parts and perform AND operation on those 4 bit input.
  //   splitter
  //   output
  //   encoder
  //   encoder
endmodule
