// Logisim project Circuit6.circ as structural Verilog: 1 circuit, main circuit main
module main (
  input  S2,
  input  S1,
  input  S0,
  input  Input_1,
  input  Input_2,
  input  Input_3,
  input  Input_4,
  input  Enable,
  input  Input_5,
  input  Input_6,
  input  Input_7,
  input  Input_8,
  output out_13
);

  wire and_1_out, and_2_out, and_3_out, and_4_out, and_5_out, and_6_out, and_7_out, and_8_out, not_1_out,
       not_2_out, not_3_out, or_1_out;

  not not_1 (not_1_out, S2);
  not not_2 (not_2_out, S1);
  not not_3 (not_3_out, S0);
  and and_1 (and_1_out, not_1_out, not_2_out, not_3_out, Input_1);
  and and_2 (and_2_out, not_1_out, not_2_out, S0, Input_2);
  and and_3 (and_3_out, not_1_out, S1, not_3_out, Input_3);
  and and_4 (and_4_out, not_1_out, S1, S0, Input_4);
  and and_5 (and_5_out, S2, not_2_out, not_3_out, Input_5);
  and and_6 (and_6_out, S2, not_2_out, S0, Input_6);
  and and_7 (and_7_out, S2, S1, not_3_out, Input_7);
  and and_8 (and_8_out, S2, S1, S0, Input_8);
  or or_1 (or_1_out, and_1_out, and_2_out, and_3_out, and_4_out, and_5_out, and_6_out, and_7_out, and_8_out);
  and and_9 (out_13, or_1_out, Enable);

  // Notes on the sheet:
  //   6.Design a circuit for 8:1 Multiplexer using gates.
endmodule
