// Logisim project Circuit7.circ as structural Verilog: 1 circuit, main circuit main
module main (
  input  Input,
  input  Enable,
  input  S0,
  input  S1,
  output out_5,
  output out_6,
  output out_7,
  output out_8
);

  wire and_1_out, not_1_out, not_2_out;

  not not_1 (not_1_out, S1);
  not not_2 (not_2_out, S0);
  and and_1 (and_1_out, Input, Enable);
  and and_2 (out_5, not_2_out, not_1_out, and_1_out);
  and and_3 (out_6, not_2_out, S1, and_1_out);
  and and_4 (out_7, S0, not_1_out, and_1_out);
  and and_5 (out_8, S0, S1, and_1_out);

  // Notes on the sheet:
  //   7.Design a circuit for 1:4 DeMultiplexer using gates.
endmodule
