// Logisim project Circuit8.circ as structural Verilog: 1 circuit, main circuit main
module main (
  input  S1,
  input  S0,
  input  in_3,
  input  in_4,
  input  in_5,
  input  in_6,
  input  in_7,
  input  in_8,
  input  Enable,
  input  in_10,
  input  in_11,
  output out_12
);

  wire adder_1_out, and_1_out, and_2_out, and_3_out, and_4_out, not_1_out, not_2_out, or_1_out,
       subtractor_1_out, xnor_1_out, xor_1_out;

  not not_1 (not_1_out, S1);
  not not_2 (not_2_out, S0);
  xor xor_1 (xor_1_out, in_3, in_4);
  Adder #(.width(1)) adder_1 (.a(in_7), .b(in_8), .out(adder_1_out));  // open: cin, cout
  Subtractor #(.width(1)) subtractor_1 (.a(in_10), .b(in_11), .out(subtractor_1_out));  // open: bin, bout
  xnor xnor_1 (xnor_1_out, in_5, in_6);
  and and_1 (and_1_out, xor_1_out, not_2_out, not_1_out);
  and and_2 (and_2_out, xnor_1_out, S0, not_1_out);
  and and_3 (and_3_out, adder_1_out, not_2_out, S1);
  and and_4 (and_4_out, subtractor_1_out, S0, S1);
  or or_1 (or_1_out, and_1_out, and_2_out, and_3_out, and_4_out);
  and and_5 (out_12, or_1_out, Enable);

  // Notes on the sheet:
  //   8.Use multiplexer circuit and give four inputs: XOR,XNOR,FULL ADDER,FULL SUBTRACTOR 
  //   FULL ADDER
  //   FULL SUBTRACTOR
  //   XOR
  //   XNOR
endmodule
