// Logisim project CO_assign_7.circ as structural Verilog: 1 circuit, main circuit main
module main (
  input  A_0,
  input  A_1,
  input  A_2,
  input  A_3,
  input  B_0,
  input  B_1,
  input  B_2,
  input  B_3,
  input  A_0_2,
  input  A_1_2,
  input  A_2_2,
  input  A_3_2,
  input  B_0_2,
  input  B_1_2,
  input  B_2_2,
  input  B_3_2,
  input  msb,
  input  a2,
  input  a1,
  input  in_20,
  input  b0,
  input  b1,
  input  b2,
  input  msb_2,
  input  in_25,
  output C_0,
  output C_1,
  output C_2,
  output C_3,
  output C_0_2,
  output C_1_2,
  output C_2_2,
  output C_3_2,
  output [7:0] out_34,
  output [7:0] out_35
);

  wire adder_1_cout, adder_2_cout, or_1_out;
  wire [0:0] adder_4_out, adder_5_out;
  wire [2:0] and_2_out;
  wire [3:0] adder_4_cout, adder_5_cout, adder_6_out, and_5_out, and_9_out, and_13_out;
  wire [7:0] and_1_out, bit_extender_1_out;

  Adder #(.width(1)) adder_1 (.a(A_0), .b(B_0), .out(C_0), .cout(adder_1_cout));  // open: cin
  Adder #(.width(1)) adder_2 (.a(A_1), .b(B_1), .out(C_1), .cin(adder_1_cout), .cout(adder_2_cout));
  Adder #(.width(1)) adder_3 (.a(A_2), .b(B_2), .out(C_2), .cin(adder_2_cout));  // open: cout
  xor xor_1 (C_3, A_3, B_3);
  Subtractor #(.width(3)) subtractor_1 (
    .a({A_2_2, A_1_2, A_0_2}), .b({B_2_2, B_1_2, B_0_2}), .out({C_2_2, C_1_2, C_0_2}));  // open: bin, bout
  xor xor_2 (C_3_2, A_3_2, B_3_2);
  and and_1 (and_1_out[0], in_20, b0);
  and and_2 (and_2_out[0], a1, b0);
  and and_3 (and_2_out[1], a2, b0);
  and and_4 (and_2_out[2], msb, b0);
  and and_5 (and_5_out[0], in_20, b1);
  and and_6 (and_5_out[1], a1, b1);
  and and_7 (and_5_out[2], a2, b1);
  and and_8 (and_5_out[3], msb, b1);
  and and_9 (and_9_out[0], in_20, b2);
  and and_10 (and_9_out[1], a1, b2);
  and and_11 (and_9_out[2], a2, b2);
  and and_12 (and_9_out[3], msb, b2);
  and and_13 (and_13_out[0], in_20, msb_2);
  and and_14 (and_13_out[1], a1, msb_2);
  and and_15 (and_13_out[2], a2, msb_2);
  and and_16 (and_13_out[3], msb, msb_2);
  or or_1 (or_1_out, msb_2, msb);
  Adder #(.width(4)) adder_4 (
    .a({1'b0, and_2_out}), .b(and_5_out), .out({adder_4_cout[2:0], adder_4_out[0]}), .cout(adder_4_cout[3]));  // open: cin
  Adder #(.width(4)) adder_5 (
    .a(adder_4_cout), .b(and_9_out), .out({adder_5_cout[2:0], adder_5_out[0]}), .cout(adder_5_cout[3]));  // open: cin
  Adder #(.width(4)) adder_6 (.a(adder_5_cout), .b(and_13_out), .out(adder_6_out), .cout(and_1_out[7]));  // open: cin
  assign bit_extender_1_out = {{7{or_1_out}}, or_1_out};  // Bit_Extender bit_extender_1
  assign out_34 = {and_1_out[7], adder_6_out, adder_5_out[0], adder_4_out[0], and_1_out[0]} ^ bit_extender_1_out;  // XOR_Gate xor_3, 8 bits wide
  Bit_Extender #(.in_width(1), .out_width(8), .\type ("input")) bit_extender_2 (
    .in(in_25), .out(out_35));  // open: extend

  // Notes on the sheet:
  //   4-bit Subractor
  //   4-bit Adder
  //   1.Implement 4 bit adder
  //   2,Implement 4 bit subtractor
  //   3,Implement 4 bit multiplier.
  //   4 BIT MULTIPLIER
  //   a0
endmodule
