// Logisim project circuit.circ as structural Verilog: 1 circuit, main circuit main
module main (
  input  [3:0] in_1,
  input  [3:0] in_2,
  input  [3:0] in_3,
  input  [3:0] in_4,
  input  [3:0] in_5,
  input  [3:0] in_6,
  input  [7:0] in_7,
  input  [3:0] in_8,
  output [3:0] out_9,
  output out_10,
  output [3:0] out_11,
  output [7:0] out_12,
  output [3:0] out_13,
  output [3:0] out_14
);

  wire adder_1_cout, subtractor_1_bout, xor_1_out;

  Multiplier #(.width(4)) multiplier_1 (.a(in_5), .b(in_6), .out(out_12[3:0]), .cin(4'b0000), .cout(out_12[7:4]));
  Divider #(.width(4)) divider_1 (.a(in_7[3:0]), .b(in_8), .out(out_13), .upper(in_7[7:4]), .rem(out_14));
  Adder #(.width(4)) adder_1 (.a(in_1), .b(in_2), .out(out_9), .cin(1'b0), .cout(adder_1_cout));
  xor xor_1 (xor_1_out, in_2[3], in_1[3]);
  Subtractor #(.width(4)) subtractor_1 (.a(in_3), .b(in_4), .out(out_11), .bin(1'b0), .bout(subtractor_1_bout));
  nand nand_1 (out_10, adder_1_cout, xor_1_out);

  // Notes on the sheet:
  //   1.
  //   2.
  //   3.
  //   4.
  //   ADDER
  //   SUBTRACTOR
  //   MULTIPLIER
  //   DIVIDER
  //   OVERFLOW
endmodule
