// Logisim project circuit.circ as structural Verilog: 1 circuit, main circuit main
module main (
  input  [7:0] in_1,
  input  [7:0] in_2,
  input  in_3,
  input  in_4,
  input  in_5,
  input  in_6,
  input  in_7,
  input  [7:0] in_8,
  input  [7:0] in_9,
  input  in_10,
  input  in_11,
  input  in_12,
  input  in_13,
  input  in_14,
  input  in_15,
  input  ENABLE,
  input  in_17,
  input  in_18,
  input  [7:0] in_19,
  input  SELECT,
  input  [3:0] in_21,
  input  in_22,
  input  in_23,
  input  SELECT_2,
  input  in_25,
  input  in_26,
  input  SELECT_3,
  input  in_28,
  output [7:0] out_29,
  output [7:0] out_30,
  output [7:0] out_31,
  output [7:0] out_32,
  output [7:0] out_33,
  output [7:0] out_34,
  output [7:0] out_35,
  output [7:0] out_36,
  output [7:0] OUTPUT_WRITTEN
);

  wire button_1_out, button_2_out, button_3_out, button_4_out, clock_1_out, clock_2_out, clock_3_out,
       controlled_buffer_1_out, controlled_buffer_2_out, controlled_buffer_3_out;
  wire [3:0] counter_1_q;
  wire [7:0] counter_2_q, counter_3_q, random_1_out, random_2_out, rom_1_data, rom_2_data;

  assign controlled_buffer_1_out = in_17 ? clock_1_out : 1'bz;  // Controlled_Buffer controlled_buffer_1
  Clock clock_1 (.out(clock_1_out));
  Counter #(.width(4), .max('hf)) counter_1 (
    .Q(counter_1_q), .clk(controlled_buffer_2_out));  // open: load, D, count, carry, clr
  assign controlled_buffer_2_out = in_28 ? clock_2_out : 1'bz;  // Controlled_Buffer controlled_buffer_2
  Clock clock_2 (.out(clock_2_out));
  Counter counter_2 (.Q(counter_2_q), .clk(controlled_buffer_3_out));  // open: load, D, count, carry, clr
  assign controlled_buffer_3_out = in_7 ? clock_3_out : 1'bz;  // Controlled_Buffer controlled_buffer_3
  Clock clock_3 (.out(clock_3_out));
  Button button_1 (.out(button_1_out));
  Counter counter_3 (.Q(counter_3_q), .clk(controlled_buffer_1_out));  // open: load, D, count, carry, clr
  Button button_2 (.out(button_2_out));
  Random random_1 (.clk(clock_1_out), .out(random_1_out));  // open: next, clr
  ROM #(.addrWidth(4)) rom_1 (.addr(in_21), .data(rom_1_data), .sel(SELECT_2));
  Random random_2 (.clk(clock_3_out), .out(random_2_out));  // open: next, clr
  ROM #(.addrWidth(4)) rom_2 (.addr(counter_1_q), .data(rom_2_data), .sel(SELECT_3));
  RAM #(.bus("separate")) ram_1 (
    .addr(in_8), .din(in_9), .data(out_31), .sel(in_10), .clk(button_1_out), .ld(in_11));  // open: str, clr
  Button button_3 (.out(button_3_out));
  Button button_4 (.out(button_4_out));
  ROM rom_3 (.addr(in_19), .data(out_35), .sel(SELECT));
  RAM #(.addrWidth(4), .bus("separate")) ram_2 (
    .addr(in_21), .din(rom_1_data), .data(out_36), .sel(in_22), .clk(button_3_out), .ld(in_23));  // open: str, clr
  RAM #(.bus("separate")) ram_3 (
    .addr(in_1), .din(in_2), .data(out_29), .sel(in_3), .clk(button_2_out), .ld(in_4));  // open: str, clr
  RAM #(.bus("separate")) ram_4 (
    .addr(counter_2_q), .din(random_2_out), .data(out_30), .sel(in_5), .clk(controlled_buffer_3_out),
    .ld(in_6));  // open: str, clr
  Register register_1 (.D(out_31), .en(in_12), .Q(out_32), .clk(button_4_out), .clr(in_13));
  RAM #(.bus("separate")) ram_5 (
    .addr(counter_3_q), .din(random_1_out), .data(out_33), .sel(in_14), .clk(controlled_buffer_1_out),
    .ld(in_15));  // open: str, clr
  Register register_2 (.D(out_33), .en(ENABLE), .Q(out_34), .clk(controlled_buffer_1_out), .clr(in_18));
  RAM #(.addrWidth(4), .bus("separate")) ram_6 (
    .addr(counter_1_q), .din(rom_2_data), .data(OUTPUT_WRITTEN), .sel(in_25), .clk(controlled_buffer_2_out),
    .ld(in_26));  // open: str, clr

  // Notes on the sheet:
  //   1.d)
  //   2.
  //   1.a) b)
  //   1.c)
  //   METHOD 1:
  //   METHOD 2:
  //   CONTROLLED BUFFER
  //   CONTROLLED BUFFER
  //   CLOCK / BUTTON
  //   ADDRESS
  //   COUNTER
  //   CLOCK
  //   METHOD 1:
  //   DATA
  //   METHOD 2:
  //   COUNTER
  //   CLOCK
  //   METHOD 1:
  //   ADDRESS
  //   DATA
  //   METHOD 2:
  //   COUNTER
  //   CLOCK
  //   ADDRESS
  //   ADDRESS
  //   BUTTON / CLOCK
  //   ROM
  //   contents of rom_1 (hex, n*v repeats v):
  //   6c 4f 5d 4a 2a 2f 9a 6c 2a 3b 3c 4d 8d 9f 5e 8f
  //   ROM
  //   contents of rom_2 (hex, n*v repeats v):
  //   6c 4f 5d 4a 2a 2f 9a 6c 2a 3b 3c 4d 8d 9f 5e 8f
  //   ASSIGNMENT 8
  //   RANDOM BIT GENERATOR
  //   RANDOM BIT GENERATOR
  //   ROM
  //   RAM
  //   CLOCK / BUTTON
  //   RAM
  //   RAM
  //   ENABLE
  //   CLOCK / BUTTON
  //   RAM
  //   CLOCK / BUTTON
  //   contents of rom_3 (hex, n*v repeats v):
  //   2 3 21 21 6*12 56 5 7 5 5 6 11 47 16 4 8 9 7 4 6 1 2 9 5 6 1 3 10 55 35 3 13 3 2 66 0 21 36 45 23 13
  //   2 0 0 1 24 25 25 23 6 54 5 6 5 6 5 6 5 6 5 56 55 56 55 54 55 54 55 54 55 54 55 5 55 54 55 54 55 54
  //   55 54 55 54 55 54 52 52 51 54 52 51 54 52 51 54 62 6 66 6 66 99 99 9 44 4 11 2 33 8 55 3 22 4 55 12
  //   2 55 5 1 2 15 5 1 2 1 2 2 1 3 1 32 0 1 32 1 3 54 18 0 36 2 1 6 5 21 35 52 2 1 5 1 3 21 3 1 0 3 23 1
  //   32 3 1 3 21 3 1 32 5 1 32 1 23 21 11 63 3 3 1 4 3 3 1 3 1 3 5 1 2 2 1 2 3 3 10 2 3 2 21 1 3 3 21 3 2
  //   5*3 43 73 1 22 62 15 23 53 61 13 31 3 22 23 63 22 33 62 63 62 63 65 65 63 63 62 63 62 33 33 63 33 63
  //   23 62 63 63 33 23 32 32 13
  //   REGISTER
  //   CLOCK
  //   OUTPUT
  //   OUTPUT
  //   RAM
  //   OUTPUT
  //   OUTPUT
  //   MAKE EVERYTHING 0
  //   OUTPUT
  //   MAKE EVERYTHING 0
  //   OUTPUT WRITTEN
endmodule
