// Logisim project CIRCUIT.circ as structural Verilog: 1 circuit, main circuit main
module main (
  input  I1,
  input  I0,
  input  Input,
  input  A1,
  input  B1,
  input  A0,
  input  B0,
  input  [1:0] A,
  input  [1:0] B,
  input  A0_2,
  input  A1_2,
  input  A2,
  input  A3,
  input  B0_2,
  input  B1_2,
  input  B2,
  input  B3,
  output O0,
  output O1,
  output O2,
  output O3,
  output A_B,
  output A_B_2,
  output A_B_3,
  output P0,
  output P1,
  output P2,
  output P3,
  output S0,
  output S1,
  output S2,
  output S3,
  output C_OUT
);

  wire adder_1_cout, adder_2_cout, adder_3_cout, and_1_out, and_2_out, and_3_out, and_4_out, and_5_out,
       and_6_out, and_7_out, and_8_out, and_14_out, and_15_out, not_1_out, not_2_out, not_3_out, not_4_out,
       not_5_out, not_6_out, xnor_1_out, xnor_2_out;

  not not_1 (not_1_out, A1);
  not not_2 (not_2_out, B1);
  not not_3 (not_3_out, I1);
  not not_4 (not_4_out, A0);
  Adder #(.width(1)) adder_1 (.a(A0_2), .b(B0_2), .out(S0), .cin(1'b0), .cout(adder_1_cout));
  not not_5 (not_5_out, I0);
  not not_6 (not_6_out, B0);
  and and_1 (and_1_out, A0, A1, not_6_out);
  and and_2 (and_2_out, A0, not_6_out, not_2_out);
  and and_3 (and_3_out, not_2_out, A1);
  xnor xnor_1 (xnor_1_out, A1, B1);
  xnor xnor_2 (xnor_2_out, A0, B0);
  and and_4 (and_4_out, not_1_out, B0);
  and and_5 (and_5_out, not_4_out, B0, not_1_out);
  and and_6 (and_6_out, not_4_out, B0, B1);
  and and_7 (and_7_out, B[0], A[1]);
  and and_8 (and_8_out, B[1], A[1]);
  Adder #(.width(1)) adder_2 (.a(A1_2), .b(B1_2), .out(S1), .cin(adder_1_cout), .cout(adder_2_cout));
  and and_9 (O0, Input, not_5_out, not_3_out);
  and and_10 (O1, Input, I0, not_3_out);
  and and_11 (O2, Input, not_5_out, I1);
  and and_12 (O3, Input, I0, I1);
  or or_1 (A_B, and_1_out, and_2_out, and_3_out);
  and and_13 (A_B_2, xnor_1_out, xnor_2_out);
  or or_2 (A_B_3, and_4_out, and_5_out, and_6_out);
  and and_14 (and_14_out, and_7_out, and_8_out);
  and and_15 (and_15_out, B[1], A[1]);
  Adder #(.width(1)) adder_3 (.a(A2), .b(B2), .out(S2), .cin(adder_2_cout), .cout(adder_3_cout));
  and and_16 (P0, B[0], A[0]);
  xor xor_1 (P1, and_7_out, and_8_out);
  xor xor_2 (P2, and_14_out, and_15_out);
  and and_17 (P3, and_14_out, and_15_out);
  Adder #(.width(1)) adder_4 (.a(A3), .b(B3), .out(S3), .cin(adder_3_cout), .cout(C_OUT));

  // Notes on the sheet:
  //   3. 2 bit multiplier circuit.
  //   1.Design a circuit for 1:4 Demultiplexer.
  //   2.Circuit for 2 bit magnitude comparator.
  //   4.Design a circuit for 4 bit binary adder.
  //   ASSIGNMENT 9
endmodule
