// Logisim project 1-4DEMUX.circ as structural Verilog: 1 circuit, main circuit main
module main (
  input  A,
  input  B,
  input  Data_Bit,
  output OUT_1,
  output OUT_2,
  output OUT_3,
  output OUT_4
);

  wire not_1_out, not_2_out;

  not not_1 (not_1_out, A);
  not not_2 (not_2_out, B);
  and and_1 (OUT_1, Data_Bit, not_2_out, not_1_out);
  and and_2 (OUT_2, Data_Bit, B, not_1_out);
  and and_3 (OUT_3, Data_Bit, not_2_out, A);
  and and_4 (OUT_4, Data_Bit, B, A);

  // Notes on the sheet:
  //   1:4 DEMULTIPLEXER
endmodule
