// Logisim project 1_BIT_HALF_SUBTRACTOR.circ as structural Verilog: 1 circuit, main circuit main
module main (
  input  in_1,
  input  in_2,
  output out_3,
  output out_4
);

  wire and_1_out, and_2_out, not_1_out, not_2_out, not_3_out;

  not not_1 (not_1_out, in_1);
  not not_2 (not_2_out, in_2);
  not not_3 (not_3_out, in_1);
  and and_1 (and_1_out, not_1_out, in_2);
  and and_2 (and_2_out, in_1, not_2_out);
  and and_3 (out_4, not_3_out, not_3_out, in_2);
  or or_1 (out_3, and_1_out, and_1_out, and_2_out, and_2_out);

  // Notes on the sheet:
  //   x0
  //   x1
  //   D
  //   c
endmodule
