// Logisim project 2_BIT_MULTIPLIER.circ as structural Verilog: 1 circuit, main circuit main
module main (
  input  A1,
  input  A0,
  input  B1,
  input  B0,
  output C3,
  output C2,
  output C1,
  output C0
);

  wire and_2_out, and_3_out, and_4_out, and_5_out;

  and and_1 (C0, A0, B0);
  and and_2 (and_2_out, A0, B1);
  and and_3 (and_3_out, B0, A1);
  and and_4 (and_4_out, B1, A1);
  and and_5 (and_5_out, and_2_out, and_3_out);
  xor xor_1 (C2, and_4_out, and_5_out);
  and and_6 (C3, and_4_out, and_5_out);
  xor xor_2 (C1, and_2_out, and_3_out);

  // Notes on the sheet:
  //   2 - BIT MULTIPLIER
endmodule
