// Logisim project 4_BIT_FULL_ADDER.circ as structural Verilog: 1 circuit, main circuit main
module main (
  input  B3,
  input  in_2,
  input  CARRY_IN,
  input  A2,
  input  B2,
  input  A1,
  input  B1,
  input  A0,
  input  B0,
  output OUT_1,
  output OUT_2,
  output OUT_3,
  output OUT_4,
  output CARRY_OUT
);

  wire and_1_out, and_2_out, and_3_out, and_4_out, and_5_out, and_6_out, and_7_out, and_8_out, or_1_out,
       or_2_out, or_3_out, xor_1_out, xor_2_out, xor_3_out, xor_4_out;

  xor xor_1 (xor_1_out, B3, in_2);
  xor xor_2 (xor_2_out, A2, B2);
  xor xor_3 (xor_3_out, A1, B1);
  xor xor_4 (xor_4_out, A0, B0);
  ExactlyOne xor_5 (.out(OUT_1), .in0(xor_1_out), .in3(CARRY_IN), .in4(CARRY_IN));
  and and_1 (and_1_out, CARRY_IN, xor_1_out);
  and and_2 (and_2_out, in_2, B3);
  and and_3 (and_3_out, or_2_out, xor_2_out);
  and and_4 (and_4_out, B2, A2);
  xor xor_6 (OUT_2, xor_2_out, or_2_out);
  or or_1 (or_1_out, and_3_out, and_3_out, and_4_out);
  xor xor_7 (OUT_3, xor_3_out, or_1_out);
  and and_5 (and_5_out, or_1_out, xor_3_out);
  and and_6 (and_6_out, B1, A1);
  xor xor_8 (OUT_4, xor_4_out, or_3_out);
  and and_7 (and_7_out, or_3_out, xor_4_out);
  and and_8 (and_8_out, B0, A0);
  or or_2 (or_2_out, and_1_out, and_1_out, and_2_out, and_2_out);
  or or_3 (or_3_out, and_5_out, and_6_out);
  or or_4 (CARRY_OUT, and_7_out, and_8_out);

  // Notes on the sheet:
  //   A3
endmodule
