// Logisim project 4_BIT_FULL_SUB.circ as structural Verilog: 1 circuit, main circuit main
module main (
  input  A3,
  input  A1,
  input  B3,
  input  B1,
  input  Bin,
  input  A2,
  input  A0,
  input  B2,
  input  B0,
  output OUT_1,
  output OUT_3,
  output OUT_2,
  output OUT_4,
  output Bout
);

  wire and_1_out, and_2_out, and_3_out, and_4_out, and_5_out, and_6_out, and_7_out, and_8_out, not_1_out,
       not_2_out, not_3_out, not_4_out, not_5_out, not_6_out, not_7_out, not_8_out, or_1_out, or_2_out,
       or_3_out, xor_1_out, xor_2_out, xor_5_out, xor_6_out;

  not not_1 (not_1_out, A3);
  xor xor_1 (xor_1_out, A3, B3);
  not not_2 (not_2_out, A2);
  and and_1 (and_1_out, B3, not_1_out);
  xor xor_2 (xor_2_out, A2, B2);
  and and_2 (and_2_out, B2, not_2_out);
  not not_3 (not_3_out, Bin);
  not not_4 (not_4_out, or_1_out);
  xor xor_3 (OUT_1, xor_1_out, Bin);
  and and_3 (and_3_out, not_3_out, xor_1_out);
  xor xor_4 (OUT_2, xor_2_out, or_1_out);
  and and_4 (and_4_out, not_4_out, xor_2_out);
  or or_1 (or_1_out, and_3_out, and_1_out);
  or or_2 (or_2_out, and_4_out, and_2_out);
  not not_5 (not_5_out, A1);
  not not_6 (not_6_out, A0);
  xor xor_5 (xor_5_out, A1, B1);
  and and_5 (and_5_out, B1, not_5_out);
  xor xor_6 (xor_6_out, A0, B0);
  and and_6 (and_6_out, B0, not_6_out);
  xor xor_7 (OUT_3, xor_5_out, or_2_out);
  not not_7 (not_7_out, or_2_out);
  and and_7 (and_7_out, not_7_out, xor_5_out);
  not not_8 (not_8_out, or_3_out);
  xor xor_8 (OUT_4, xor_6_out, or_3_out);
  and and_8 (and_8_out, not_8_out, xor_6_out);
  or or_3 (or_3_out, and_7_out, and_5_out);
  or or_4 (Bout, and_8_out, and_6_out);

  // Notes on the sheet:
  //   OUT-1
endmodule
