// Logisim project 4_BIT_HALF_ADDER.circ as structural Verilog: 1 circuit, main circuit main
module main (
  input  A3,
  input  A1,
  input  B,
  input  A2,
  input  A0,
  output OUT_1,
  output OUT_3,
  output OUT_2,
  output OUT_4,
  output CARRY_OUT
);

  wire and_1_out, and_2_out, and_3_out;

  xor xor_1 (OUT_1, A3, B);
  and and_1 (and_1_out, B, A3);
  xor xor_2 (OUT_2, A2, and_1_out);
  and and_2 (and_2_out, and_1_out, A2);
  xor xor_3 (OUT_3, A1, and_2_out);
  and and_3 (and_3_out, and_2_out, A1);
  xor xor_4 (OUT_4, A0, and_3_out);
  and and_4 (CARRY_OUT, and_3_out, A0);
endmodule
