// Logisim project 4_BIT_HALF_SUB.circ as structural Verilog: 1 circuit, main circuit main
module main (
  input  A3,
  input  A1,
  input  B,
  input  A2,
  input  A0,
  output OUT_1,
  output OUT_3,
  output OUT_2,
  output OUT_4,
  output Bout
);

  wire and_1_out, and_2_out, and_3_out, not_1_out, not_2_out, not_3_out, not_4_out;

  not not_1 (not_1_out, A3);
  not not_2 (not_2_out, A2);
  xor xor_1 (OUT_1, A3, B);
  and and_1 (and_1_out, B, not_1_out);
  xor xor_2 (OUT_2, A2, and_1_out);
  and and_2 (and_2_out, and_1_out, not_2_out);
  xor xor_3 (OUT_3, A1, and_2_out);
  not not_3 (not_3_out, A1);
  xor xor_4 (OUT_4, A0, and_3_out);
  not not_4 (not_4_out, A0);
  and and_3 (and_3_out, and_2_out, not_3_out);
  and and_4 (Bout, and_3_out, not_4_out);
endmodule
