// Logisim project 8_BIT_FULL_ADDER.circ as structural Verilog: 1 circuit, main circuit main
module main (
  input  A3,
  input  A7,
  input  B3,
  input  B7,
  input  CARRY_IN,
  input  A2,
  input  A6,
  input  B2,
  input  B6,
  input  A1,
  input  A5,
  input  B1,
  input  B5,
  input  A4,
  input  A0,
  input  B4,
  input  B0,
  output OUT_5,
  output OUT_1,
  output OUT_6,
  output OUT_2,
  output OUT_7,
  output OUT_3,
  output OUT_4,
  output OUT_8,
  output CARRY_OUT
);

  wire and_1_out, and_2_out, and_3_out, and_4_out, and_5_out, and_6_out, and_7_out, and_8_out, and_9_out,
       and_10_out, and_11_out, and_12_out, and_13_out, and_14_out, and_15_out, and_16_out, or_1_out,
       or_2_out, or_3_out, or_4_out, or_5_out, or_7_out, or_8_out, xor_1_out, xor_2_out, xor_3_out,
       xor_4_out, xor_9_out, xor_10_out, xor_11_out, xor_12_out;

  xor xor_1 (xor_1_out, A7, B7);
  xor xor_2 (xor_2_out, A6, B6);
  xor xor_3 (xor_3_out, A5, B5);
  xor xor_4 (xor_4_out, A4, B4);
  xor xor_5 (OUT_1, xor_1_out, CARRY_IN);
  and and_1 (and_1_out, CARRY_IN, xor_1_out);
  and and_2 (and_2_out, B7, A7);
  xor xor_6 (OUT_2, xor_2_out, or_1_out);
  and and_3 (and_3_out, or_1_out, xor_2_out);
  and and_4 (and_4_out, B6, A6);
  xor xor_7 (OUT_3, xor_3_out, or_2_out);
  and and_5 (and_5_out, or_2_out, xor_3_out);
  and and_6 (and_6_out, B5, A5);
  xor xor_8 (OUT_4, xor_4_out, or_3_out);
  and and_7 (and_7_out, or_3_out, xor_4_out);
  and and_8 (and_8_out, B4, A4);
  or or_1 (or_1_out, and_1_out, and_2_out);
  or or_2 (or_2_out, and_3_out, and_4_out);
  or or_3 (or_3_out, and_5_out, and_6_out);
  or or_4 (or_4_out, and_7_out, and_8_out);
  xor xor_9 (xor_9_out, A3, B3);
  xor xor_10 (xor_10_out, A2, B2);
  xor xor_11 (xor_11_out, A1, B1);
  xor xor_12 (xor_12_out, A0, B0);
  and and_9 (and_9_out, or_4_out, xor_9_out);
  and and_10 (and_10_out, B3, A3);
  and and_11 (and_11_out, or_8_out, xor_11_out);
  and and_12 (and_12_out, B1, A1);
  and and_13 (and_13_out, or_5_out, xor_12_out);
  and and_14 (and_14_out, B0, A0);
  xor xor_13 (OUT_5, xor_9_out, or_4_out);
  xor xor_14 (OUT_6, xor_10_out, or_7_out);
  and and_15 (and_15_out, or_7_out, xor_10_out);
  and and_16 (and_16_out, B2, A2);
  xor xor_15 (OUT_7, xor_11_out, or_8_out);
  or or_5 (or_5_out, and_11_out, and_12_out);
  xor xor_16 (OUT_8, xor_12_out, or_5_out);
  or or_6 (CARRY_OUT, and_13_out, and_14_out);
  or or_7 (or_7_out, and_9_out, and_10_out);
  or or_8 (or_8_out, and_15_out, and_16_out);
endmodule
