// Logisim project 8_BIT_FULL_SUB.circ as structural Verilog: 1 circuit, main circuit main
module main (
  input  A7,
  input  A3,
  input  B7,
  input  B3,
  input  Bin,
  input  A6,
  input  A2,
  input  B6,
  input  B2,
  input  A5,
  input  A1,
  input  B5,
  input  B1,
  input  A4,
  input  A0,
  input  B4,
  input  B0,
  output OUT_1,
  output OUT_5,
  output OUT_2,
  output OUT_6,
  output OUT_3,
  output OUT_7,
  output OUT_4,
  output OUT_8,
  output Bout
);

  wire and_1_out, and_2_out, and_3_out, and_4_out, and_5_out, and_6_out, and_7_out, and_8_out, and_9_out,
       and_10_out, and_11_out, and_12_out, and_13_out, and_14_out, and_15_out, and_16_out, not_1_out,
       not_2_out, not_3_out, not_4_out, not_5_out, not_6_out, not_7_out, not_8_out, not_9_out, not_10_out,
       not_11_out, not_12_out, not_13_out, not_14_out, not_15_out, not_16_out, or_1_out, or_2_out, or_3_out,
       or_4_out, or_5_out, or_6_out, or_7_out, xor_1_out, xor_2_out, xor_3_out, xor_4_out, xor_9_out,
       xor_10_out, xor_11_out, xor_12_out;

  not not_1 (not_1_out, A7);
  not not_2 (not_2_out, A6);
  not not_3 (not_3_out, A5);
  xor xor_1 (xor_1_out, A7, B7);
  xor xor_2 (xor_2_out, A6, B6);
  xor xor_3 (xor_3_out, A5, B5);
  not not_4 (not_4_out, A4);
  and and_1 (and_1_out, B7, not_1_out);
  and and_2 (and_2_out, B6, not_2_out);
  and and_3 (and_3_out, B5, not_3_out);
  xor xor_4 (xor_4_out, A4, B4);
  and and_4 (and_4_out, B4, not_4_out);
  not not_5 (not_5_out, Bin);
  not not_6 (not_6_out, or_1_out);
  not not_7 (not_7_out, or_2_out);
  not not_8 (not_8_out, or_3_out);
  xor xor_5 (OUT_1, xor_1_out, Bin);
  and and_5 (and_5_out, not_5_out, xor_1_out);
  xor xor_6 (OUT_2, xor_2_out, or_1_out);
  and and_6 (and_6_out, not_6_out, xor_2_out);
  xor xor_7 (OUT_3, xor_3_out, or_2_out);
  and and_7 (and_7_out, not_7_out, xor_3_out);
  xor xor_8 (OUT_4, xor_4_out, or_3_out);
  and and_8 (and_8_out, not_8_out, xor_4_out);
  or or_1 (or_1_out, and_5_out, and_1_out);
  or or_2 (or_2_out, and_6_out, and_2_out);
  or or_3 (or_3_out, and_7_out, and_3_out);
  or or_4 (or_4_out, and_8_out, and_4_out);
  not not_9 (not_9_out, A2);
  not not_10 (not_10_out, A1);
  not not_11 (not_11_out, A0);
  not not_12 (not_12_out, A3);
  xor xor_9 (xor_9_out, A2, B2);
  xor xor_10 (xor_10_out, A1, B1);
  and and_9 (and_9_out, B1, not_10_out);
  xor xor_11 (xor_11_out, A0, B0);
  and and_10 (and_10_out, B0, not_11_out);
  xor xor_12 (xor_12_out, A3, B3);
  and and_11 (and_11_out, B3, not_12_out);
  and and_12 (and_12_out, B2, not_9_out);
  not not_13 (not_13_out, or_4_out);
  not not_14 (not_14_out, or_5_out);
  xor xor_13 (OUT_7, xor_10_out, or_6_out);
  not not_15 (not_15_out, or_6_out);
  and and_13 (and_13_out, not_15_out, xor_10_out);
  xor xor_14 (OUT_8, xor_11_out, or_7_out);
  not not_16 (not_16_out, or_7_out);
  and and_14 (and_14_out, not_16_out, xor_11_out);
  xor xor_15 (OUT_5, xor_12_out, or_4_out);
  and and_15 (and_15_out, not_13_out, xor_12_out);
  xor xor_16 (OUT_6, xor_9_out, or_5_out);
  and and_16 (and_16_out, not_14_out, xor_9_out);
  or or_5 (or_5_out, and_15_out, and_11_out);
  or or_6 (or_6_out, and_16_out, and_12_out);
  or or_7 (or_7_out, and_13_out, and_9_out);
  or or_8 (Bout, and_14_out, and_10_out);
endmodule
